# Fritzing sketch matrix_setup (saved by Fritzing 0.9.4)

parts:
  Part1 = NeoPixel NeoMatrix 8x8 [part_number=1487]
  Part3 = Adafruit Feather RP2040 [part_number="Adafruit #4884"]

nets:
  N1: Part1.IN, Part3.VBAT
  N2: Part1.VDD, Part3.D12
  GND: Part1.GND, Part3.GND

custom parts:
  NeoPixel NeoMatrix 8x8: Put on your sunglasses before wiring up this LED matrix - 64 eye-blistering RGB LEDs adorn the NeoMatrix for a blast of configurable color. Arranged in an 8x8 matrix, each pixel is individually addressable. Only one microcontroller pin is required to control all the LEDs, and you get 24 bit color for each LED.
  Adafruit Feather RP2040: A new chip means a new Feather, and the Raspberry Pi RP2040 is no exception. When we saw this chip we thought "this chip is going to be awesome when we give it the Feather Treatment" and so we did! This Feather features the RP2040, and all niceties you know and love about Feather Measures 2.0" x 0.9" x 0.28" (50.8mm x 22.8mm x 7mm) without headers soldered in Light as a (large?) feather - 5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
